# Fritzing sketch schematic (saved by Fritzing 0.9.3b)
circuit board: 8.46667cm x 5.64444cm
perfboards: 1

parts:
  JP2 = Header 12 [package=1x12_machine-pin-header_lock.004]
  JP3 = Header 12 [package=1x12_machine-pin-header_lock.004]
  Part3 = Photon
  VCC4 = Battery block 9V
  M2 = DC Motor
  SPKR3 = Loudspeaker
  Part4 = Breakout Board for Electret Microphone
  tone_buzzer = Piezo Speaker
  eyeled = LED - 5mm [color="Infrared (850nm)" package="5 mm [THT]"]
  S5 = Toggle Switch [package=THT]
  hc-sr2 = hc-sr04
  U2 = mystery part, 6 pins [chip_label=H-Bridge]
  J4 = Screw terminal - 2 pins [package=THT]
  S7 = Square Pushbutton
  Part5 = Adafruit PAM8302 [part_number="Adafruit #2130"]
  S8 = Toggle Switch [package=THT]
  J5 = Basic Servo  # not connected
  U4 = Battery Holders [package=lipo-1100mAh]
  Part7 = Power Cell LiPo Charger/Booster

nets:
  N1: JP2.2, Part3.VIN
  N2: JP2.3, JP3.5, Part3.GND
  N3: JP2.4, Part3.TX
  N4: JP2.5, Part3.RX
  N5: JP2.6, Part3.WKP, tone_buzzer.pin2
  N6: JP2.7, Part3.DAC, Part4.AUD
  N7: JP2.8, Part3.A5
  N8: JP2.9, Part3.A4, eyeled.anode
  N9: JP2.10, Part3.A3
  N10: JP2.11, Part3.A2
  N11: JP2.12, Part3.A1
  N12: JP3.2, Part3.3V3
  N13: JP3.3, Part3.RST
  N14: JP3.4, Part3.VBAT
  N15: JP3.6, Part3.D7
  N16: JP3.7, Part3.D6
  N17: JP3.8, Part3.D5, hc-sr2.Echo
  N18: JP3.9, Part3.D4, hc-sr2.Trig
  N19: JP3.10, Part3.D3, S7.leg0
  N20: JP3.11, Part3.D2, U2.pin1
  N21: JP3.12, Part3.D1, U2.pin2
  N22: VCC4.+, S8.L2
  N23: M2.pin_1, U2.pin6, J4.pin1
  N24: M2.pin_2, U2.pin5
  N25: SPKR3.pin1, Part5.VO+
  N26: SPKR3.pin2, Part5.VO-
  N27: S5.L1, S5.COM
  N28: S5.L2, Part7.5VIN
  N29: U2.pin3, S8.COM
  N30: U4.+, Part7.VCC
  N31: U4.-, Part7.GND

notes:
  Front Passthrough
  Lower
  Eyes Servo
  Upper
  VCC
  GND
  Tone Piezo
  Microphone
  Listen Button
  Ping Sensor
  Speaker
  Drive Motor
  Main Power Li-poly
  Li-poly Charger
  Drive Battery

custom parts:
  Adafruit PAM8302: This super small mono amplifier is surprisingly powerful - able to deliver up to 2.5 Watts into 4-8 ohm impedance speakers. Inside the miniature chip is a class D controller, able to run from 2.0V-5.5VDC. Since the amp is a class D, its very efficient (over 90% efficient when driving an 8Ω speaker at over half a Watt) - making it perfect for portable and battery-powered projects. It has built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
